# Fritzing sketch NodeMCUv3 (saved by Fritzing 0.9.10b)

parts:
  U1 = NodeMCU V3.0
  J1 = Piezo Speaker  # not connected
  LED1 = LED - 5mm [color="Green (560nm)" current=0.030 package="5 mm [THT]"]  # not connected
  LED2 = LED - 5mm [color="Red (633nm)" current=0.030 package="5 mm [THT]"]  # not connected
  LED3 = LED - 5mm [color="Blue (505nm)" current=0.030 package="5 mm [THT]"]  # not connected
  LED4 = LED - 5mm [color="Yellow (585nm)" current=0.030 package="5 mm [THT]"]  # not connected
  S5 = Pushbutton [package=THT]
  S6 = Pushbutton [package=THT]
  S7 = Pushbutton [package=THT]
  S8 = Pushbutton [package=THT]

nets:
  N1: U1.D4, S5.leg1
  N2: U1.D5, S8.leg1
  N3: U1.D6, S7.leg1
  N4: U1.D7, S6.leg1

custom parts:
  NodeMCU V3.0: ESP8266 based NodeMCU
